# Fritzing sketch modular-led-mosfet-flipped (saved by Fritzing 0.9.3b)
circuit board: 4.76061cm x 3.01239cm
breadboards: 1

parts:
  OptoIso = Sharp PC817 [package=THT]
  part = Resistor [tolerance=±5% resistance=33k package=THT]
  part_2 = Resistor [tolerance=±5% resistance=500 package=THT]
  +pwm = Camdenboss CTB0158-2 [part_number=CTB0158-2 package=THT]
  !!!_---_+++ = Camdenboss CTB0158-3 [part_number=CTB0158-3 package=THT]
  +input-_-output+ = Camdenboss CTB0158-4 [part_number=CTB0158-4 package=THT]

nets:
  N1: OptoIso.Pin_1, part_2.Pin_1
  N2: OptoIso.Pin_2, +pwm.pin1
  N3: OptoIso.Pin_4, part.Pin_0, !!!_---_+++.pin1
  N4: OptoIso.Pin_3, !!!_---_+++.pin3, +input-_-output+.pin2
  N5: part.Pin_1, +input-_-output+.pin1, +input-_-output+.pin4
  N6: part_2.Pin_0, +pwm.pin2
  N7: !!!_---_+++.pin2, +input-_-output+.pin3

notes:
  pin 1
  pin 3
  Gnd
  Vcc
  +
  -
  output
  input

custom parts:
  Camdenboss CTB0158-2: Camdenboss CTB0158-2 5.08mm (0.2") Pitch Standard Profile 90 ̊ Rising Clamp Terminal, 2 pole The real-life connectors are modular, made up of two or three connector blocks slotted together. These can be further slotted together to make larger connectors. Fritzing part is derived from Screw terminals by Lionel Michel. Because of the offset between connection pins and screw terminals, these are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
