# Fritzing sketch modular-led-mosfet-rgb (saved by Fritzing 0.9.3b)
circuit board: 8.46667cm x 5.64444cm
breadboards: 1

parts:
  U1 = Sharp PC817 [package=THT]
  U2 = Sharp PC817 [package=THT]
  U3 = Sharp PC817 [package=THT]
  R1 = Resistor [tolerance=±5% resistance=500 package=THT]
  R2 = Resistor [tolerance=±5% resistance=500 package=THT]
  R3 = Resistor [tolerance=±5% resistance=500 package=THT]
  PWM = Camdenboss CTB0158-4 [part_number=CTB0158-4 package=THT]
  HighPower = Camdenboss CTB0158-3 [part_number=CTB0158-3 package=THT]
  GreenOut = Camdenboss CTB0158-2 [part_number="Green out" package=THT]
  BlueOut = Camdenboss CTB0158-2 [part_number="blue Out" package=THT]
  RedOut = Camdenboss CTB0158-2 [part_number="Red out" package=THT]
  RedFET = Camdenboss CTB0158-3 [part_number=CTB0158-3 package=THT]
  GreenFet = Camdenboss CTB0158-3 [part_number=CTB0158-3 package=THT]
  BlueFet = Camdenboss CTB0158-3 [part_number=CTB0158-3 package=THT]
  R4 = Resistor [tolerance=±5% resistance=33 package=THT]
  R5 = Resistor [tolerance=±5% resistance=33 package=THT]
  R6 = Resistor [tolerance=±5% resistance=33 package=THT]

nets:
  N1: U1.Pin_1, R1.Pin_1
  N2: U1.Pin_2, U2.Pin_2, U3.Pin_2, PWM.pin1
  N3: U1.Pin_4, RedFET.pin1, R4.Pin_0
  N4: U1.Pin_3, HighPower.pin3, RedFET.pin3
  N5: U2.Pin_1, R2.Pin_1
  N6: U2.Pin_4, GreenFet.pin1, R5.Pin_0
  N7: U2.Pin_3, GreenFet.pin3
  N8: U3.Pin_1, R3.Pin_1
  N9: U3.Pin_4, BlueFet.pin1, R6.Pin_0
  N10: U3.Pin_3, BlueFet.pin3
  N11: R1.Pin_0, PWM.pin4
  N12: R2.Pin_0, PWM.pin3
  N13: R3.Pin_0, PWM.pin2
  N14: HighPower.pin1, RedOut.pin1, R4.Pin_1
  N15: HighPower.pin2, GreenOut.pin1, BlueOut.pin1, R5.Pin_1, R6.Pin_1
  N16: GreenOut.pin2, GreenFet.pin2
  N17: BlueOut.pin2, BlueFet.pin2
  N18: RedOut.pin2, RedFET.pin2
