# Fritzing sketch 12v5v-breakout (saved by Fritzing 0.9.3b)
circuit board: 3.17188cm x 2.11017cm
breadboards: 1

parts:
  12v = female pin header, 3 pins [form="♀ (female)"]
  5v = female pin header, 3 pins [form="♀ (female)"]
  36v = female pin header, 2 pins [form="♀ (female)"]
  5v-out = female pin header, 2 pins [form="♀ (female)"]
  12v-out = female pin header, 2 pins [form="♀ (female)"]

nets:
  N1: 12v.pin1, 36v.pin1, 12v-out.pin2
  N2: 12v.pin2, 5v.pin2, 36v.pin2, 5v-out.pin2, 12v-out.pin1
  N3: 12v.pin3, 5v.pin3
  N4: 5v.pin1, 5v-out.pin1

notes:
  1 2 3
  +  -
  + -
