# Fritzing sketch breakout (saved by Fritzing 0.9.3b)
circuit board: 2.1cm x 3.4cm
breadboards: 1

parts:
  ETH_OUT = RJ45 Jack [package=rj45-8]
  PIN_IN = shrouded pin header, 8 pins [form="♂ (shrouded male)"]

nets:
  N1: ETH_OUT.1, PIN_IN.pin1
  N2: ETH_OUT.2, PIN_IN.pin2
  N3: ETH_OUT.3, PIN_IN.pin3
  N4: ETH_OUT.4, PIN_IN.pin4
  N5: ETH_OUT.5, PIN_IN.pin5
  N6: ETH_OUT.6, PIN_IN.pin6
  N7: ETH_OUT.7, PIN_IN.pin7
  N8: ETH_OUT.8, PIN_IN.pin8
