# Fritzing sketch esp32-breakout (1) (saved by Fritzing 0.9.3b)
circuit board: 2.5679cm x 5.5108cm
breadboards: 1

parts:
  esp32 = female pin header, 20 pins [form="♀ (female)"]
  5vin = female pin header, 3 pins [form="♀ (female)"]
  1 = female pin header, 4 pins [form="♀ (female)"]
  2 = female pin header, 4 pins [form="♀ (female)"]
  3 = female pin header, 4 pins [form="♀ (female)"]
  4 = female pin header, 4 pins [form="♀ (female)"]
  dyn = female pin header, 2 pins [form="♀ (female)"]
  12vin = female pin header, 2 pins [form="♀ (female)"]
  3v-led = female pin header, 2 pins [form="♀ (female)"]

nets:
  N1: esp32.pin1, 3v-led.pin1
  N2: esp32.pin2, 1.pin1, 2.pin1, 3.pin1, 4.pin1, dyn.pin1, 3v-led.pin2
  N3: esp32.pin4, 1.pin2
  N4: esp32.pin5, 1.pin3
  N5: esp32.pin6, 1.pin4
  N6: esp32.pin7, 2.pin2
  N7: esp32.pin8, 2.pin3
  N8: esp32.pin9, 2.pin4
  N9: esp32.pin10, 3.pin2
  N10: esp32.pin11, 3.pin3
  N11: esp32.pin12, 3.pin4
  N12: esp32.pin13, 4.pin2
  N13: esp32.pin14, 4.pin3
  N14: esp32.pin15, 4.pin4
  N15: esp32.pin16, esp32.pin17, dyn.pin2
  N16: esp32.pin19, 5vin.pin2, 12vin.pin1
  N17: esp32.pin20, 5vin.pin3
  N18: 5vin.pin1, 12vin.pin2

notes:
  3.3v
  gnd
  gpio5
  gpio6
  gpio7
  gpio8
  gpio10
  gpio16
  gpio11
  gpio9
  gpi34
  gpi39
  gpio32
  gpio17
  gpio33
  gpi35
  5v
  gpi36
  esp-en
  - r g b
