# Fritzing sketch esp32-breakout (saved by Fritzing 0.9.3b)
circuit board: 5.29997cm x 5.7cm
breadboards: 1

parts:
  part = double row female pin header, 38 pins [form="♀ (female)"]
  J2 = double row female pin header, 38 pins [form="♀ (female)"]
  3_3vin = female pin header, 3 pins [form="♀ (female)"]
  part_2 = female pin header, 17 pins [form="♀ (female)"]

nets:
  N1: part.pin1, part.pin38, 3_3vin.pin2
  N2: part.pin2, part.pin37
  N3: part.pin3, part.pin36
  N4: part.pin4, part.pin35
  N5: part.pin5, part.pin34
  N6: part.pin6, part.pin33
  N7: part.pin7, part.pin32, part_2.pin2
  N8: part.pin8, part.pin31, part_2.pin3
  N9: part.pin9, part.pin30, part_2.pin4
  N10: part.pin10, part.pin29, part_2.pin5
  N11: part.pin11, part.pin28, part_2.pin6
  N12: part.pin12, part.pin27, part_2.pin7
  N13: part.pin13, part.pin26, part_2.pin8
  N14: part.pin14, part.pin25, 3_3vin.pin3, part_2.pin16
  N15: part.pin15, part.pin24, part_2.pin9
  N16: part.pin16, part.pin23
  N17: part.pin17, part.pin22
  N18: part.pin18, part.pin21
  N19: part.pin19, part.pin20
  N20: J2.pin1, J2.pin38, part_2.pin1
  N21: J2.pin2, J2.pin37, part_2.pin11
  N22: J2.pin3, J2.pin36, part_2.pin12
  N23: J2.pin4, J2.pin5, J2.pin34, J2.pin35, part_2.pin14, part_2.pin15
  N24: J2.pin6, J2.pin33, part_2.pin13
  N25: J2.pin7, J2.pin32
  N26: J2.pin8, J2.pin31
  N27: J2.pin9, J2.pin30
  N28: J2.pin10, J2.pin29
  N29: J2.pin11, J2.pin28
  N30: J2.pin12, J2.pin27
  N31: J2.pin13, J2.pin26
  N32: J2.pin14, J2.pin25
  N33: J2.pin15, J2.pin24, part_2.pin10
  N34: J2.pin16, J2.pin23
  N35: J2.pin17, J2.pin22
  N36: J2.pin18, J2.pin21
  N37: J2.pin19, J2.pin20
  N38: 3_3vin.pin1, part_2.pin17

notes:
  3v3
  en
  36
  39
  34
  35
  33
  32
  25
  26
  14
  9
  27
  12
  13
  gnd
  11
  10
  5v
  23
  0
  19
  21
  sd0
  22
  2
  18
  17
  4
  rx
  16
  tx
  clk
  sd1
  5
  15
  B1
  B4
  G2
  out
  G1
  G4
  B3
  R3
  B2
  G3
  R1
  R2
  vin
  R4
