# Fritzing sketch eth-breakout (saved by Fritzing 0.9.3b)
circuit board: 2.12916cm x 4.14345cm
breadboards: 1

parts:
  eth-out = RJ45 Jack [package=rj45-8]
  out-in = shrouded pin header, 8 pins [form="♂ (shrouded male)"]
  1_2_3 = female pin header, 3 pins [form="♀ (female)"]

nets:
  N1: eth-out.1, 1_2_3.pin1
  N2: eth-out.2, out-in.pin2
  N3: eth-out.3, out-in.pin3
  N4: eth-out.4, out-in.pin4, 1_2_3.pin2
  N5: eth-out.5, out-in.pin5
  N6: eth-out.6, out-in.pin6
  N7: eth-out.7, out-in.pin7
  N8: eth-out.8, out-in.pin8
  N9: out-in.pin1, 1_2_3.pin3
