# Fritzing sketch mb-test (saved by Fritzing 0.9.3b)
circuit board: 4.34238cm x 3.66414cm
breadboards: 1

parts:
  +_- = shrouded pin header, 6 pins [form="♂ (shrouded male)"]
  +_-_2 = shrouded pin header, 6 pins [form="♂ (shrouded male)"]
  +_-_3 = shrouded pin header, 6 pins [form="♂ (shrouded male)"]
  B_G_R_- = female pin header, 4 pins [form="♀ (female)"]
  R_G_B_- = female pin header, 4 pins [form="♀ (female)"]
  IN = Camdenboss CTB0158-2 [part_number=CTB0158-2 package=THT]

nets:
  N1: +_-.pin1, B_G_R_-.pin2
  N2: +_-.pin2, +_-_2.pin2, +_-_3.pin2, IN.pin1
  N3: +_-.pin3, R_G_B_-.pin3
  N4: +_-.pin4, +_-_2.pin4, +_-_3.pin4, R_G_B_-.pin1
  N5: +_-.pin5, +_-_2.pin5, +_-_3.pin5, IN.pin2
  N6: +_-.pin6, +_-_2.pin6, +_-_3.pin6, B_G_R_-.pin4
  N7: +_-_2.pin1, B_G_R_-.pin3
  N8: +_-_2.pin3, R_G_B_-.pin4
  N9: +_-_3.pin1, B_G_R_-.pin1
  N10: +_-_3.pin3, R_G_B_-.pin2

notes:
  p i o
  PWM
  OUT
  + -

custom parts:
  Camdenboss CTB0158-2: Camdenboss CTB0158-2 5.08mm (0.2") Pitch Standard Profile 90 ̊ Rising Clamp Terminal, 2 pole The real-life connectors are modular, made up of two or three connector blocks slotted together. These can be further slotted together to make larger connectors. Fritzing part is derived from Screw terminals by Lionel Michel. Because of the offset between connection pins and screw terminals, these are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
