# Fritzing sketch sm-msft1.6 (saved by Fritzing 0.9.3b)
circuit board: 2.3cm x 3.1cm
breadboards: 1

parts:
  G_D_S = STP16NF06 N-Channel Power MOSFET
  Opto = Sharp PC817 [package=THT]
  part = Resistor [tolerance=±5% resistance=33k package=THT]
  part_2 = Resistor [tolerance=±5% resistance=33k package=THT]
  500 = Resistor [tolerance=±5% resistance=500 package=THT]
  +_- = shrouded pin header, 6 pins [form="♂ (shrouded male)"]

nets:
  N1: G_D_S.gate, Opto.Pin_4, part.Pin_0, part_2.Pin_0
  N2: G_D_S.drain, +_-.pin4
  N3: G_D_S.source, Opto.Pin_3, part_2.Pin_1, +_-.pin5
  N4: Opto.Pin_1, 500.Pin_1
  N5: Opto.Pin_2, +_-.pin6
  N6: part.Pin_1, +_-.pin2, +_-.pin3
  N7: 500.Pin_0, +_-.pin1

notes:
  p i o

custom parts:
  STP16NF06 N-Channel Power MOSFET: STP16NF06 N-channel Power MOSFET
