# Fritzing sketch together-test (saved by Fritzing 0.9.3b)
circuit board: 10cm x 10cm
breadboards: 1

parts:
  +_- = shrouded pin header, 6 pins [form="♂ (shrouded male)"]
  +_-_2 = shrouded pin header, 6 pins [form="♂ (shrouded male)"]
  +_-_3 = shrouded pin header, 6 pins [form="♂ (shrouded male)"]
  OUT2 = shrouded pin header, 8 pins [form="♂ (shrouded male)"]
  +_-_4 = shrouded pin header, 6 pins [form="♂ (shrouded male)"]
  +_-_5 = shrouded pin header, 6 pins [form="♂ (shrouded male)"]
  OUT1 = shrouded pin header, 8 pins [form="♂ (shrouded male)"]
  +_-_6 = shrouded pin header, 6 pins [form="♂ (shrouded male)"]
  +_-_7 = shrouded pin header, 6 pins [form="♂ (shrouded male)"]
  +_-_8 = shrouded pin header, 6 pins [form="♂ (shrouded male)"]
  +_-_9 = shrouded pin header, 6 pins [form="♂ (shrouded male)"]
  OUT3 = shrouded pin header, 8 pins [form="♂ (shrouded male)"]
  +_-_10 = shrouded pin header, 6 pins [form="♂ (shrouded male)"]
  OUT4 = shrouded pin header, 8 pins [form="♂ (shrouded male)"]
  +_-_11 = shrouded pin header, 6 pins [form="♂ (shrouded male)"]
  +_-_12 = shrouded pin header, 6 pins [form="♂ (shrouded male)"]
  5vreg = female pin header, 3 pins [form="♀ (female)"]
  + = female pin header, 3 pins [form="♀ (female)"]
  - = female pin header, 3 pins [form="♀ (female)"]
  12vin = female pin header, 2 pins [form="♀ (female)"]
  36vin = female pin header, 2 pins [form="♀ (female)"]
  esp32 = female pin header, 13 pins [form="♀ (female)"]
  5vin = female pin header, 2 pins [form="♀ (female)"]
  dyn = female pin header, 2 pins [form="♀ (female)"]

nets:
  N1: +_-.pin1, esp32.pin7
  N2: +_-.pin2, +_-_2.pin2, +_-_3.pin2, +_-_4.pin2, +_-_5.pin2, +_-_6.pin2, +_-_8.pin2, +_-_9.pin2, +_-_11.pin2, +.pin1, +.pin2, +.pin3, 36vin.pin2
  N3: +_-.pin3, +_-_2.pin3, +_-_3.pin3, OUT2.pin1, OUT2.pin8
  N4: +_-.pin4, OUT2.pin4
  N5: +_-.pin5, +_-_2.pin5, +_-_3.pin5, +_-_4.pin5, +_-_5.pin5, +_-_6.pin5, +_-_7.pin5, +_-_8.pin5, +_-_9.pin5, +_-_10.pin5, +_-_11.pin5, +_-_12.pin5, -.pin1, -.pin2, -.pin3, 36vin.pin1
  N6: +_-.pin6, +_-_2.pin6, +_-_3.pin6, +_-_4.pin6, +_-_5.pin6, +_-_6.pin6, +_-_7.pin6, +_-_8.pin6, +_-_9.pin6, +_-_10.pin6, +_-_11.pin6, +_-_12.pin6, esp32.pin1
  N7: +_-_2.pin1, esp32.pin5
  N8: +_-_2.pin4, OUT2.pin2
  N9: +_-_3.pin1, esp32.pin6
  N10: +_-_3.pin4, OUT2.pin3
  N11: OUT2.pin5, OUT1.pin5, OUT3.pin5, OUT4.pin5, dyn.pin1, dyn.pin2
  N12: OUT2.pin6, OUT1.pin6, OUT3.pin6, OUT4.pin6, 5vreg.pin2, 12vin.pin2, 5vin.pin1
  N13: OUT2.pin7, OUT1.pin7, OUT3.pin7, OUT4.pin7, 5vreg.pin1, 12vin.pin1
  N14: +_-_4.pin1, esp32.pin4
  N15: +_-_4.pin3, +_-_5.pin3, OUT1.pin1, OUT1.pin8, +_-_6.pin3
  N16: +_-_4.pin4, OUT1.pin4
  N17: +_-_5.pin1, esp32.pin2
  N18: +_-_5.pin4, OUT1.pin2
  N19: OUT1.pin3, +_-_6.pin4
  N20: +_-_6.pin1, esp32.pin3
  N21: +_-_7.pin1, esp32.pin10
  N22: +_-_7.pin2, +_-_10.pin2, +_-_12.pin2
  N23: +_-_7.pin3, +_-_10.pin3, OUT4.pin1, OUT4.pin8, +_-_12.pin3
  N24: +_-_7.pin4, OUT4.pin4
  N25: +_-_8.pin1, esp32.pin13
  N26: +_-_8.pin3, +_-_9.pin3, OUT3.pin1, OUT3.pin8, +_-_11.pin3
  N27: +_-_8.pin4, OUT3.pin4
  N28: +_-_9.pin1, esp32.pin11
  N29: +_-_9.pin4, OUT3.pin2
  N30: OUT3.pin3, +_-_11.pin4
  N31: +_-_10.pin1, esp32.pin8
  N32: +_-_10.pin4, OUT4.pin2
  N33: OUT4.pin3, +_-_12.pin4
  N34: +_-_11.pin1, esp32.pin12
  N35: +_-_12.pin1, esp32.pin9
  N36: 5vreg.pin3, 5vin.pin2

notes:
  p i o R
  + -
  V G S
  - B G R
  p i o G
  p i o B
  B G R -
  tx
  G
  G3
  R4
  B3
  rx
  R3
  G2
  B4
  G4
  R2
  B2
  R1
  G1
  B1
  7RNX
